# Fritzing sketch simonsGame_schema (saved by Fritzing 0.9.4)
breadboards: 1

parts:
  Part1 = Arduino Uno (Rev3)
  LCD1 = LCD screen
  LED1 = LED - 5mm [color="Red (633nm)" package="5 mm [THT]"]
  LED2 = LED - 5mm [color="Blue (430nm)" package="5 mm [THT]"]
  LED3 = LED - 5mm [color="Yellow (585nm)" package="5 mm [THT]"]
  LED4 = LED - 5mm [color="Green (555nm)" package="5 mm [THT]"]
  R4 = Resistor [tolerance=±5% resistance=10k package=THT]
  S1 = Pushbutton [package="[THT]"]  # not connected
  R7 = Photocell (LDR) [package=THT]
  R9 = Photocell (LDR) [package=THT]
  R10 = Photocell (LDR) [package=THT]
  R11 = Photocell (LDR) [package=THT]
  R12 = Resistor [tolerance=±5% resistance=220 package=THT]
  R13 = Resistor [tolerance=±5% resistance=220 package=THT]
  R14 = Resistor [tolerance=±5% resistance=220 package=THT]
  R15 = Resistor [tolerance=±5% resistance=220 package=THT]
  R16 = Resistor [tolerance=±5% resistance=220 package=THT]
  R17 = Resistor [tolerance=±5% resistance=220 package=THT]
  R18 = Resistor [tolerance=±5% resistance=220 package=THT]
  R19 = Resistor [tolerance=±5% resistance=220 package=THT]
  R1 = Rotary Potentiometer (Small) [maximum_resistance=10kΩ package=THT]
  J1 = Piezo Speaker

nets:
  N1: Part1.A0, R11.pin_1, R12.Pin_0
  N2: Part1.A1, R7.pin_1, R13.Pin_0
  N3: Part1.A2, R10.pin_1, R15.Pin_0
  N4: Part1.A3, R9.pin_1, R14.Pin_0
  N5: Part1.D8, LCD1.E
  N6: Part1.D9_PWM, LCD1.DB4
  N7: Part1.D10_PWM/SS, LCD1.DB5
  N8: Part1.D11_PWM/MOSI, J1.pin2
  N9: Part1.D12/MISO, LCD1.DB6
  N10: Part1.D13/SCK, LCD1.DB7
  N11: Part1.D2, LED2.anode
  N12: Part1.D3_PWM, LED3.anode
  N13: Part1.D4, LED4.anode
  N14: Part1.D5_PWM, LED1.anode
  N15: Part1.D6_PWM, R4.Pin_1
  N16: Part1.D7, LCD1.RS
  GND: Part1.GND, LCD1.VSS, LCD1.R/W, LCD1.LED-, R4.Pin_0, R12.Pin_1, R13.Pin_1, R14.Pin_1, R15.Pin_1, R16.Pin_1, R17.Pin_1, R18.Pin_1, R19.Pin_1, R1.leg1, J1.pin1
  N17: LCD1.VDD, LCD1.LED+, R7.pin_0, R9.pin_0, R10.pin_0, R11.pin_0, R1.leg2
  N18: LCD1.V0, R1.wiper
  N19: LED1.cathode, R19.Pin_0
  N20: LED2.cathode, R17.Pin_0
  N21: LED3.cathode, R16.Pin_0
  N22: LED4.cathode, R18.Pin_0
